// Logisim project FSMcompletosincrono2.circ as structural Verilog: 1 circuit, main circuit main
module main (
);

  wire and_1_out, and_2_out, and_3_out, and_4_out, button_1_out, clock_1_out, d_ff_1_q, not_1_out, or_1_out,
       Q1_q, Q1_qn, Q2_q, Q2_qn;

  Button button_1 (.out(button_1_out));
  Clock clock_1 (.out(clock_1_out));
  not not_1 (not_1_out, button_1_out);
  D_Flip_Flop d_ff_1 (.clk(clock_1_out), .D(button_1_out), .Q(d_ff_1_q));  // open: Qn, preset, en, reset
  or or_1 (or_1_out, not_1_out, Q2_q);
  and and_1 (and_1_out, button_1_out, Q1_qn);
  and and_2 (and_2_out, Q1_qn, or_1_out);
  D_Flip_Flop Q1 (.clk(clock_1_out), .D(and_2_out), .Q(Q1_q), .Qn(Q1_qn));  // open: preset, en, reset
  D_Flip_Flop Q2 (.clk(clock_1_out), .D(and_1_out), .Q(Q2_q), .Qn(Q2_qn));  // open: preset, en, reset
  and and_3 (and_3_out, Q1_qn, Q2_qn);
  and and_4 (and_4_out, and_3_out, d_ff_1_q);
  LED Verde (.in(Q2_q));
  LED Giallo (.in(Q1_q));
  LED Rosso (.in(and_4_out));

  // Notes on the sheet:
  //   Enabled attivo alto:; ossia quando il pulsante è premuto!
  //   Codifica stati: 11 Verde Giallo; 10 Verde; 00 Rosso; 01 GialloRosso credo....
endmodule
