// Logisim project FSM.circ as structural Verilog: 1 circuit, main circuit main
module main (
);

  wire and_1_out, and_2_out, clock_1_out, Q1_q, Q1_qn, Q2_q, Q2_qn;

  Clock clock_1 (.out(clock_1_out));
  D_Flip_Flop Q1 (.clk(clock_1_out), .D(and_1_out), .Q(Q1_q), .Qn(Q1_qn));  // open: preset, en, reset
  D_Flip_Flop Q2 (.clk(clock_1_out), .D(Q1_qn), .Q(Q2_q), .Qn(Q2_qn));  // open: preset, en, reset
  and and_1 (and_1_out, Q1_qn, Q2_q);
  and and_2 (and_2_out, Q1_qn, Q1_qn, Q2_qn, Q2_qn);
  LED Verde (.in(Q2_q));
  LED Giallo (.in(Q1_q));
  LED Rosso (.in(and_2_out));

  // Notes on the sheet:
  //   Codifica stati: 11 Verde Giallo; 10 Verde; 00 Rosso; 01 Giallo credo....
endmodule
