// Logisim project FSMcompletosincronodef.circ as structural Verilog: 1 circuit, main circuit main
module main (
);

  wire and_1_out, and_2_out, and_3_out, and_4_out, clock_1_out, Enable_out, nand_1_out, or_1_out, Q0_q,
       Q0_qn, Q1_q, Q1_qn, Q2_q;

  Clock clock_1 (.out(clock_1_out));
  Button Enable (.out(Enable_out));
  nand nand_1 (nand_1_out, Enable_out, Enable_out);
  or or_1 (or_1_out, Q1_q, nand_1_out);
  and and_1 (and_1_out, Q0_qn, or_1_out);
  and and_2 (and_2_out, Q0_qn, Enable_out);
  D_Flip_Flop Q0 (.clk(clock_1_out), .D(and_1_out), .Q(Q0_q), .Qn(Q0_qn));  // open: preset, en, reset
  D_Flip_Flop Q1 (.clk(clock_1_out), .D(and_2_out), .Q(Q1_q), .Qn(Q1_qn));  // open: preset, en, reset
  D_Flip_Flop Q2 (.clk(clock_1_out), .D(Enable_out), .Q(Q2_q));  // open: Qn, preset, en, reset
  and and_3 (and_3_out, Q1_qn, Q0_qn);
  and and_4 (and_4_out, and_3_out, Q2_q);
  LED LV (.in(Q1_q));
  LED LG (.in(Q0_q));
  LED LR (.in(and_4_out));

  // Notes on the sheet:
  //   D0 = (E'+Q1).Q0'
  //   D1=Q0'.E
  //   D2=E
  //   Codifica stati: 11 Verde Giallo; 10 Verde; 00 Rosso; 01 Giallo
  //   LV=Q1
  //   LG=Q0
  //   LR=(Q0'.Q1').Q2
endmodule
