// Logisim project FSMdef.circ as structural Verilog: 1 circuit, main circuit main
module main (
);

  wire A1_out, A2_out, clock_1_out, Q0_q, Q0_qn, Q1_q, Q1_qn;

  Clock clock_1 (.out(clock_1_out));
  and A1 (A1_out, Q0_qn, Q1_q);
  D_Flip_Flop Q0 (.clk(clock_1_out), .D(A1_out), .Q(Q0_q), .Qn(Q0_qn));  // open: preset, en, reset
  D_Flip_Flop Q1 (.clk(clock_1_out), .D(Q0_qn), .Q(Q1_q), .Qn(Q1_qn));  // open: preset, en, reset
  and A2 (A2_out, Q1_qn, Q0_qn);
  LED LV (.in(Q1_q));
  LED LG (.in(Q0_q));
  LED LR (.in(A2_out));

  // Notes on the sheet:
  //   D0 = Q0'.Q1
  //   D1=Q0'
  //   Codifica stati: 11 Verde Giallo; 10 Verde; 00 Rosso; 01 Giallo
  //   LV=Q1
  //   LG=Q0
  //   LR=Q0'.Q1'
endmodule
